# Fritzing sketch Open Sensor no light (saved by Fritzing 1.0.1rc)
circuit board: 8.46667cm x 5.64444cm
stripboards: 1

parts:
  A1 = Wemos-s2-mini_1 [part_number="WeMos D1 Mini Lite"]
  Q2 = NPN-Transistor [package="TO92 [THT]"]
  BAT1 = Battery Holders [package=battery-aa]
  S1 = SWITCH-MOMENTARY-2 [package=reed_switch_pth]
  R5 = Resistor [tolerance=±5% power=0.25 resistance=22k package=THT]
  R6 = Resistor [tolerance=±5% power=0.25 resistance=22k package=THT]

nets:
  N1: A1.connector3, R5.Pin_0, R6.Pin_1
  N2: A1.connector16, BAT1.+, R6.Pin_0
  N3: A1.connector17, Q2.E, BAT1.-, S1.1
  N4: A1.connector19, S1.2
  N5: A1.connector23, A1.connector31, Q2.B
  N6: Q2.C, R5.Pin_1

notes:
  BATTERY_SENSOR_PIN=7
  OPEN_SENSOR_PIN=18
