# Fritzing sketch motion (saved by Fritzing 0.9.6b)
circuit board: 8.46667cm x 5.64444cm
stripboards: 1

parts:
  A1 = Wemos-s2-mini_1 [part_number="WeMos D1 Mini Lite"]
  R1 = Photocell (LDR) [package=THT]
  R4 = Resistor [tolerance=±5% resistance=4.7k package="0402 [SMD]"]
  Q2 = NPN-Transistor [package="TO92 [THT]"]
  R5 = Resistor [tolerance=±5% power=0.25 resistance=22k package=THT]
  BAT1 = Battery Holders [package=battery-aa]
  R8 = Resistor [tolerance=±5% power=0.25 resistance=22k package=THT]
  Part1 = PIR D-SUN HC-SR501
  BAT2 = Battery Holders [package=battery-aa]

nets (from the breadboard view):
  N1: A1.connector2, R1.pin_0, R4.Pin_1
  N2: A1.connector3, R5.Pin_1, R8.Pin_0
  N3: A1.connector7, R4.Pin_0
  N4: A1.connector16, R5.Pin_0, BAT1.+, BAT2.-
  N5: A1.connector17, Q2.E, BAT1.-, Part1.connector2
  N6: A1.connector20, Part1.connector1
  N7: A1.connector23, Q2.B
  N8: R1.pin_1, Q2.C, R8.Pin_1
  N9: Part1.connector0, BAT2.+
